# Fritzing sketch robot_heart (saved by Fritzing 0.9.3b)
breadboards: 1

parts:
  J1 = Basic Servo
  WeMos_D1_Mini1 = WeMos D1 Mini
  S1 = Magnetic Door Switch [package=reed_switch_plastic]
  R1 = Resistor [tolerance=±5% resistance=1k package="0805 [SMD]"]
  R2 = Resistor [tolerance=±5% resistance=1k package="0805 [SMD]"]
  R3 = Resistor [tolerance=±5% resistance=1k package="0805 [SMD]"]
  LED1 = RGB LED - (4 legs) [package="5 mm [THT]"]

nets:
  N1: J1.gnd, WeMos_D1_Mini1.G, S1.1
  VCC: J1.vcc, WeMos_D1_Mini1.5V
  N2: J1.pulse, WeMos_D1_Mini1.D0
  N3: WeMos_D1_Mini1.3V3, LED1.common_anode
  N4: WeMos_D1_Mini1.D3, S1.2
  N5: WeMos_D1_Mini1.D6, R3.Pin_0, R3.Pin_1, LED1.blue_cathode
  N6: WeMos_D1_Mini1.D7, R2.Pin_0, R2.Pin_1, LED1.green_cathode
  N7: WeMos_D1_Mini1.D8, R1.Pin_0, R1.Pin_1, LED1.red_cathode

notes:
  Magnetic Switch
  Heart Servo and LED
